# Fritzing sketch mini (saved by Fritzing 0.8.7b)
breadboards: 1

parts:
  Part1 = Spark Core (v1.0)
  R1 = Resistor [tolerance=±5% resistance=270 package=THT]
  R2 = Resistor [tolerance=±5% resistance=270 package=THT]
  R3 = Resistor [tolerance=±5% resistance=270 package=THT]
  LED1 = RGB LED (com. cathode, rbg) [package="5 mm [THT]"]

nets:
  N1: Part1.A5, R3.Pin_1
  N2: Part1.A6, R1.Pin_1
  N3: Part1.A7, R2.Pin_1
  N4: Part1.GND, LED1.common_cathode
  N5: R1.Pin_0, LED1.blue_anode
  N6: R2.Pin_0, LED1.red_anode
  N7: R3.Pin_0, LED1.green_anode
