# Fritzing sketch spark (saved by Fritzing 0.8.7b)
breadboards: 1

parts:
  Part1 = Spark Core (v1.0)
  LED1 = RGB LED (com. anode, rbg) [package="5 mm [THT]"]
  R1 = Resistor [tolerance=±5% resistance=270 package=THT]
  R2 = Resistor [tolerance=±5% resistance=270 package=THT]
  R3 = Resistor [tolerance=±5% resistance=270 package=THT]

nets:
  N1: Part1.A5, R1.Pin_0
  N2: Part1.A6, R2.Pin_0
  N3: Part1.A7, R3.Pin_0
  N4: Part1.GND, LED1.common_anode
  N5: LED1.red_cathode, R1.Pin_1
  N6: LED1.blue_cathode, R2.Pin_1
  N7: LED1.green_cathode, R3.Pin_1
